# Fritzing sketch CircuitDiagram (saved by Fritzing 0.9.3b)
breadboards: 1

parts:
  Arduino_Nano = Arduino Nano (Rev3.0)
  Speaker = Loudspeaker
  R = Resistor [tolerance=±5% resistance=470 package=THT]

nets:
  N1: Arduino_Nano.D2, R.Pin_0
  GND/Left Thumb/Right Thumb: Arduino_Nano.GND, Speaker.pin2
  5V: Arduino_Nano.5V
  Right Small Finger: Arduino_Nano.A7
  Right Ring Finger: Arduino_Nano.A6
  Right Middle Finger: Arduino_Nano.A5
  Right Index Finger: Arduino_Nano.A4
  Left Index Finger: Arduino_Nano.A3
  Left Middle Finger: Arduino_Nano.A2
  Left Ring Finger: Arduino_Nano.A1
  Left Small Finger: Arduino_Nano.A0
  N2: Speaker.pin1, R.Pin_1
